# Fritzing sketch Wiring Keamanan Rumah Dengan IR Obstacle (saved by Fritzing 0.9.5d)
breadboards: 1

parts:
  S1 = Momentary Switch [package=ksa_sealed_tac_switch]
  M1 = fc-51 [package=THT]
  WeMos_D1_Mini1 = WeMos D1 Mini  # not connected
  J1 = Piezo Speaker

nets:
  N1: S1.3, M1.pin2
  N2: M1.pin3, J1.pin2
